# Fritzing sketch arduino uno-ADXL345 (saved by Fritzing 0.9.3b)
breadboards: 1

parts:
  Part2 = Triple Axis Accelerometer Breakout - ADXL345
  Part3 = Triple Axis Accelerometer Breakout - ADXL345
  Part4 = Arduino Uno (Rev3)

nets:
  GND: Part2.GND, Part3.GND, Part4.GND
  VCC: Part2.VCC, Part3.VCC, Part3.SDO, Part4.5V
  N1: Part2.SDA, Part3.SDA, Part4.A4/SDA
  N2: Part2.SCL, Part3.SCL, Part4.A5/SCL

notes:
  Unit 1 0x53
  Unit 2
  0x1D
  SD0 -> shorted to VCC
  A4 - SDA
  A5 - SCL
  5V - VCC
  GND - GND
